// Logisim project T006_datapath.circ as structural Verilog: 3 circuits, main circuit main
module main (
);

  wire clock_1_out, MD;
  wire [2:0] OP;
  wire [3:0] Const, DR, S1_R;
  wire [7:0] adder_1_out, alu_1_output, bit_extender_1_out, Bus_y, Bus_z, counter_1_q, multiplexer_1_out;

  Adder adder_1 (.a(counter_1_q), .b(8'h1), .out(adder_1_out));  // open: cin, cout
  assign bit_extender_1_out = {{4{1'b0}}, Const};  // Bit_Extender bit_extender_1
  alu alu_1 (.A(Bus_y), .B(multiplexer_1_out), .\output (alu_1_output), .Selection(OP));
  Multiplexer #(.width(8), .enable("false")) multiplexer_1 (
    .in0(bit_extender_1_out), .in1(Bus_z), .out(multiplexer_1_out), .sel(MD));
  Counter counter_1 (.D(adder_1_out), .count(1'b1), .Q(counter_1_q), .clk(clock_1_out));  // open: load, carry, clr
  Clock clock_1 (.out(clock_1_out));
  ROM #(.dataWidth(16)) rom_1 (.addr(counter_1_q), .data({OP, MD, DR, S1_R, Const}));  // open: sel
  Register_files RegFiles (
    .RZ(Const), .RY(S1_R), .BusZ(Bus_z), .Rx(DR), .RegWrite(1'b1), .BusY(Bus_y), .BusX(alu_1_output));

  // Other names for the same wires on the sheet: S2_R[3:0] = Const

  // Notes on the sheet:
  //   Laith Amro 1230018 Saleem Daqa 1230060 Tala Shareef 1230346
  //   Constast
  //   PC counter hooked with a clock and a constant and its output is used as an input for the adder
  //   ROM memeory that hold our team value used is Laith Amro ID "1230018" and the team number is T006
  //   Here we used the previous block the ALU and the regFiles and connected them using all parts of the project as shown above in order to produce a fully functional circuit
  //   contents of rom_1 (hex, n*v repeats v):
  //   6 ff92 1 e 17 e ff87 ff97 ffa7 ffb7 ffc7
  //   Here we distributed the output of the ROM using a splitter into different tunnels vased on the instruction set you gave us
endmodule

module Register_files (
  input  [3:0] RZ,
  input  [3:0] RY,
  input  [7:0] BusZ,
  input  [3:0] Rx,
  input  RegWrite,
  input  [7:0] BusY,
  input  [7:0] BusX
);

  wire and_1_out, and_2_out, and_3_out, and_4_out, and_5_out, and_6_out, and_7_out, and_8_out, and_9_out,
       and_10_out, and_11_out, and_12_out, and_13_out, and_14_out, clock_out, decoder_1_out0, decoder_2_out0,
       decoder_2_out1, decoder_2_out2, decoder_2_out3, decoder_2_out4, decoder_2_out5, decoder_2_out6,
       decoder_2_out7, decoder_2_out8, decoder_2_out9, decoder_2_out10, decoder_2_out11, decoder_2_out12,
       decoder_2_out13, decoder_2_out14, decoder_2_out15, decoder_3_out0, decoder_3_out1, decoder_3_out2,
       decoder_3_out3, decoder_3_out4, decoder_3_out5, decoder_3_out6, decoder_3_out7, decoder_3_out8,
       decoder_3_out9, decoder_3_out10, decoder_3_out11, decoder_3_out12, decoder_3_out13, decoder_3_out14,
       decoder_3_out15, r1, r2, r3, r4, r5, r6, r7, r8, r9, r10, r11, r12, r14, r15;
  wire [7:0] R1_q;

  Decoder #(.select(4), .enable("false")) decoder_1 (
    .out0(decoder_1_out0), .out1(r1), .out2(r2), .out3(r3), .out4(r4), .out5(r5), .out6(r6), .out7(r7),
    .out8(r8), .out9(r9), .out10(r10), .out11(r11), .out12(r12), .out14(r14), .out15(r15), .sel(Rx));  // open: out13
  and and_1 (and_1_out, r1, RegWrite);
  and and_2 (and_2_out, r2, RegWrite);
  and and_3 (and_3_out, r3, RegWrite);
  and and_4 (and_4_out, r4, RegWrite);
  and and_5 (and_5_out, r5, RegWrite);
  and and_6 (and_6_out, r6, RegWrite);
  buf and_7 (and_7_out, r7);  // AND_Gate
  buf and_8 (and_8_out, r8);  // AND_Gate
  and and_9 (and_9_out, r9, RegWrite);
  and and_10 (and_10_out, r10, RegWrite);
  and and_11 (and_11_out, r11, RegWrite);
  and and_12 (and_12_out, r12, RegWrite);
  and and_13 (and_13_out, r14, RegWrite);
  and and_14 (and_14_out, r15, RegWrite);
  Clock clock (.out(clock_out));
  Register u_R1 (.D(BusX), .en(and_1_out), .Q(R1_q), .clk(clock_out));  // open: clr
  Register u_R2 (.D(BusX), .en(and_2_out), .Q(R1_q), .clk(clock_out));  // open: clr
  Register u_R3 (.D(BusX), .en(and_3_out), .Q(R1_q), .clk(clock_out));  // open: clr
  Register u_R4 (.D(BusX), .en(and_4_out), .Q(R1_q), .clk(clock_out));  // open: clr
  Register u_R5 (.D(BusX), .en(and_5_out), .Q(R1_q), .clk(clock_out));  // open: clr
  Register u_R6 (.D(BusX), .en(and_6_out), .Q(R1_q), .clk(clock_out));  // open: clr
  Register u_R7 (.D(BusX), .en(and_7_out), .Q(R1_q), .clk(clock_out));  // open: clr
  Register u_R8 (.D(BusX), .en(and_8_out), .Q(R1_q), .clk(clock_out));  // open: clr
  Register u_R9 (.D(BusX), .en(and_9_out), .Q(R1_q), .clk(clock_out));  // open: clr
  Register u_R10 (.D(BusX), .en(and_10_out), .Q(R1_q), .clk(clock_out));  // open: clr
  Register u_R11 (.D(BusX), .en(and_11_out), .Q(R1_q), .clk(clock_out));  // open: clr
  Register u_R12 (.D(BusX), .en(and_12_out), .Q(R1_q), .clk(clock_out));  // open: clr
  Register R13 (.D(BusX), .Q(R1_q), .clk(clock_out));  // open: en, clr
  Register u_R14 (.D(BusX), .en(and_13_out), .Q(R1_q), .clk(clock_out));  // open: clr
  Register u_R15 (.D(BusX), .en(and_14_out), .Q(R1_q), .clk(clock_out));  // open: clr
  assign BusY = decoder_2_out1 ? R1_q : 8'bz;  // Controlled_Buffer controlled_buffer_1
  assign BusY = decoder_2_out2 ? R1_q : 8'bz;  // Controlled_Buffer controlled_buffer_2
  assign BusY = decoder_2_out3 ? R1_q : 8'bz;  // Controlled_Buffer controlled_buffer_3
  assign BusY = decoder_2_out4 ? R1_q : 8'bz;  // Controlled_Buffer controlled_buffer_4
  assign BusY = decoder_2_out5 ? R1_q : 8'bz;  // Controlled_Buffer controlled_buffer_5
  assign BusY = decoder_2_out6 ? R1_q : 8'bz;  // Controlled_Buffer controlled_buffer_6
  assign BusY = decoder_2_out7 ? R1_q : 8'bz;  // Controlled_Buffer controlled_buffer_7
  assign BusY = decoder_2_out8 ? R1_q : 8'bz;  // Controlled_Buffer controlled_buffer_8
  assign BusY = decoder_2_out9 ? R1_q : 8'bz;  // Controlled_Buffer controlled_buffer_9
  assign BusY = decoder_2_out10 ? R1_q : 8'bz;  // Controlled_Buffer controlled_buffer_10
  assign BusY = decoder_2_out11 ? R1_q : 8'bz;  // Controlled_Buffer controlled_buffer_11
  assign BusY = decoder_2_out12 ? R1_q : 8'bz;  // Controlled_Buffer controlled_buffer_12
  assign BusY = decoder_2_out13 ? R1_q : 8'bz;  // Controlled_Buffer controlled_buffer_13
  assign BusY = decoder_2_out14 ? R1_q : 8'bz;  // Controlled_Buffer controlled_buffer_14
  assign BusY = decoder_2_out15 ? R1_q : 8'bz;  // Controlled_Buffer controlled_buffer_15
  Decoder #(.select(4)) decoder_2 (
    .out0(decoder_2_out0), .out1(decoder_2_out1), .out2(decoder_2_out2), .out3(decoder_2_out3),
    .out4(decoder_2_out4), .out5(decoder_2_out5), .out6(decoder_2_out6), .out7(decoder_2_out7),
    .out8(decoder_2_out8), .out9(decoder_2_out9), .out10(decoder_2_out10), .out11(decoder_2_out11),
    .out12(decoder_2_out12), .out13(decoder_2_out13), .out14(decoder_2_out14), .out15(decoder_2_out15),
    .sel(RY));  // open: en
  assign BusY = decoder_2_out0 ? {8{1'b0}} : 8'bz;  // Controlled_Buffer controlled_buffer_16
  Decoder #(.select(4)) decoder_3 (
    .out0(decoder_3_out0), .out1(decoder_3_out1), .out2(decoder_3_out2), .out3(decoder_3_out3),
    .out4(decoder_3_out4), .out5(decoder_3_out5), .out6(decoder_3_out6), .out7(decoder_3_out7),
    .out8(decoder_3_out8), .out9(decoder_3_out9), .out10(decoder_3_out10), .out11(decoder_3_out11),
    .out12(decoder_3_out12), .out13(decoder_3_out13), .out14(decoder_3_out14), .out15(decoder_3_out15),
    .sel(RZ));  // open: en
  assign BusZ = decoder_3_out0 ? {8{1'b0}} : 8'bz;  // Controlled_Buffer controlled_buffer_17
  assign BusZ = decoder_3_out1 ? R1_q : 8'bz;  // Controlled_Buffer controlled_buffer_18
  assign BusZ = decoder_3_out2 ? R1_q : 8'bz;  // Controlled_Buffer controlled_buffer_19
  assign BusZ = decoder_3_out3 ? R1_q : 8'bz;  // Controlled_Buffer controlled_buffer_20
  assign BusZ = decoder_3_out4 ? R1_q : 8'bz;  // Controlled_Buffer controlled_buffer_21
  assign BusZ = decoder_3_out5 ? R1_q : 8'bz;  // Controlled_Buffer controlled_buffer_22
  assign BusZ = decoder_3_out6 ? R1_q : 8'bz;  // Controlled_Buffer controlled_buffer_23
  assign BusZ = decoder_3_out7 ? R1_q : 8'bz;  // Controlled_Buffer controlled_buffer_24
  assign BusZ = decoder_3_out8 ? R1_q : 8'bz;  // Controlled_Buffer controlled_buffer_25
  assign BusZ = decoder_3_out9 ? R1_q : 8'bz;  // Controlled_Buffer controlled_buffer_26
  assign BusZ = decoder_3_out10 ? R1_q : 8'bz;  // Controlled_Buffer controlled_buffer_27
  assign BusZ = decoder_3_out11 ? R1_q : 8'bz;  // Controlled_Buffer controlled_buffer_28
  assign BusZ = decoder_3_out12 ? R1_q : 8'bz;  // Controlled_Buffer controlled_buffer_29
  assign BusZ = decoder_3_out13 ? R1_q : 8'bz;  // Controlled_Buffer controlled_buffer_30
  assign BusZ = decoder_3_out14 ? R1_q : 8'bz;  // Controlled_Buffer controlled_buffer_31
  assign BusZ = decoder_3_out15 ? R1_q : 8'bz;  // Controlled_Buffer controlled_buffer_32

  // Notes on the sheet:
  //   Tunnels for easier wire handeling
  //   This is our design for file register that will be used in further steps
  //   Tunnels for easier wire handeling
  //   AND GATES
endmodule

// ALU
module alu (
  input  [7:0] A,
  input  [7:0] B,
  input  [2:0] Selection,
  output [7:0] \output 
);

  wire [7:0] adder_1_out, AND_GATE_out, OR_GATE_out, subtractor_1_out, XOR_GATE_out;

  Adder adder_1 (.a(B), .b(A), .out(adder_1_out));  // open: cin, cout
  Subtractor subtractor_1 (.a(B), .b(A), .out(subtractor_1_out));  // open: bin, bout
  assign AND_GATE_out = B & A;  // AND_Gate AND_GATE, 8 bits wide
  assign OR_GATE_out = B | A;  // OR_Gate OR_GATE, 8 bits wide
  assign XOR_GATE_out = B ^ A;  // XOR_Gate XOR_GATE, 8 bits wide
  Multiplexer #(.select(3), .width(8)) multiplexer_1 (
    .in0(adder_1_out), .in1(subtractor_1_out), .in2(AND_GATE_out), .in3(OR_GATE_out), .in4(XOR_GATE_out),
    .out(\output ), .sel(Selection));  // open: in5, in6, in7, en

  // Notes on the sheet:
  //   This is design of the ALU circuit that will be used in further steps
endmodule
